// Logisim project ALU.circ as structural Verilog
module ALU (
  input  [31:0] A,
  input  [31:0] B,
  input  [4:0] Shift,
  input  [3:0] Codop,
  input  CarryIn,
  input  in_6,
  input  [31:0] in_7,
  output [31:0] S,
  output [3:0] Flags
);

  wire not_1_out, subtractor_1_bout;
  wire [31:0] adder_1_out, and_1_out, negator_1_out, shifter_1_out, shifter_2_out, shifter_3_out,
       shifter_4_out, subtractor_1_out, TST, xor_1_out;

  Comparator #(.width(32)) comparator_1 (.a(in_7), .b(TST), .gt(Flags[0]), .eq(Flags[1]));  // open: lt
  not not_1 (not_1_out, CarryIn);
  not not_2 (Flags[2], subtractor_1_bout);
  Subtractor #(.width(32)) subtractor_1 (
    .a(A), .b(B), .out(subtractor_1_out), .bin(not_1_out), .bout(subtractor_1_bout));
  assign and_1_out = A & B;  // AND_Gate and_1, 32 bits wide
  assign xor_1_out = A ^ B;  // XOR_Gate xor_1, 32 bits wide
  Shifter #(.width(32)) shifter_1 (.in(B), .\dist (Shift), .out(shifter_1_out));
  Shifter #(.shift("lr"), .width(32)) shifter_2 (.in(B), .\dist (Shift), .out(shifter_2_out));
  Shifter #(.shift("ar"), .width(32)) shifter_3 (.in(B), .\dist (Shift), .out(shifter_3_out));
  Shifter #(.shift("rl"), .width(32)) shifter_4 (.in(B), .\dist (Shift), .out(shifter_4_out));
  Negator #(.width(32)) negator_1 (.in(A), .out(negator_1_out));
  Adder #(.width(32)) adder_1 (.a(A), .b(B), .out(adder_1_out), .cin(CarryIn), .cout(Flags[2]));
  assign TST = A & B;  // AND_Gate and_2, 32 bits wide
  Multiplexer #(.select(4), .width(32)) multiplexer_1 (
    .in0(and_1_out), .in1(xor_1_out), .in2(shifter_1_out), .in3(shifter_2_out), .in4(shifter_3_out),
    .in5(adder_1_out), .in6(subtractor_1_out), .in7(shifter_4_out), .in8(in_7), .in9(negator_1_out), .out(S),
    .sel(Codop));  // open: in10, in11, in12, in13, in14, in15

  // Other names for the same wires on the sheet: Cero[31:0] = in_7; Cero1Bit = in_6; cIn = CarryIn; N = Flags[0];
  //   Z = Flags[1]; C = Flags[2]; V = Flags[3]

  // Notes on the sheet:
  //   Note: for ROR, C = N
  //   Note 2: assume that shift > 0 for LSL and LSR
endmodule
